// Logisim project Somador.circ as structural Verilog
module meioSomador (
  input  A,
  input  B,
  output S,
  output Cout
);

  xor xor_1 (S, A, B);
  and and_1 (Cout, A, B);
endmodule

module somadorCompleto (
  input  A,
  input  B,
  input  Cin,
  output S,
  output Cout
);

  wire meiosomador_1_cout, meiosomador_1_s, meiosomador_2_cout;

  meioSomador meiosomador_1 (.A(A), .B(B), .S(meiosomador_1_s), .Cout(meiosomador_1_cout));
  meioSomador meiosomador_2 (.A(meiosomador_1_s), .B(Cin), .S(S), .Cout(meiosomador_2_cout));
  or or_1 (Cout, meiosomador_2_cout, meiosomador_1_cout);
endmodule

module meioSubtrator (
  input  A,
  input  B,
  output S,
  output Tout
);

  xor xor_1 (S, A, B);
  and and_1 (Tout, B, ~A);  // AND_Gate
endmodule

module subtratorCompleto (
  input  A,
  input  B,
  input  Tin,
  output S,
  output Tout
);

  wire meiosubtrator_1_s, meiosubtrator_1_tout, meiosubtrator_2_tout;

  meioSubtrator meiosubtrator_1 (.A(A), .B(B), .S(meiosubtrator_1_s), .Tout(meiosubtrator_1_tout));
  meioSubtrator meiosubtrator_2 (.A(meiosubtrator_1_s), .B(Tin), .S(S), .Tout(meiosubtrator_2_tout));
  or or_1 (Tout, meiosubtrator_2_tout, meiosubtrator_1_tout);
endmodule

module Final (
  input  [1:0] A,
  input  [1:0] B,
  input  Op,
  output [1:0] S
);

  wire [1:0] somadorcompletao_1_s, subtratorcompletao_1_s;

  somadorCompletao somadorcompletao_1 (.A(A), .B(B), .S(somadorcompletao_1_s));
  subtratorCompletao subtratorcompletao_1 (.A(A), .B(B), .S(subtratorcompletao_1_s));
  Multiplexer #(.width(2), .enable("false")) multiplexer_1 (
    .in0(somadorcompletao_1_s), .in1(subtratorcompletao_1_s), .out(S), .sel(Op));

  // Notes on the sheet:
  //   0 - Soma
  //   1 - Subtrai
endmodule

module somadorCompletao (
  input  [1:0] A,
  input  [1:0] B,
  output [1:0] S
);

  wire somadorcompleto_2_cout;

  somadorCompleto somadorcompleto_1 (.A(A[1]), .B(B[1]), .Cin(somadorcompleto_2_cout), .S(S[1]));  // open: Cout
  somadorCompleto somadorcompleto_2 (.A(A[0]), .B(B[0]), .Cin(1'b0), .S(S[0]), .Cout(somadorcompleto_2_cout));
endmodule

module subtratorCompletao (
  input  [1:0] A,
  input  [1:0] B,
  output [1:0] S
);

  wire subtratorcompleto_2_tout;

  subtratorCompleto subtratorcompleto_1 (.A(A[1]), .B(B[1]), .Tin(subtratorcompleto_2_tout), .S(S[1]));  // open: Tout
  subtratorCompleto subtratorcompleto_2 (.A(A[0]), .B(B[0]), .Tin(1'b0), .S(S[0]), .Tout(subtratorcompleto_2_tout));
endmodule
