// Logisim project multiplicar.circ as structural Verilog
module meioSomador (
  input  A,
  input  B,
  output S,
  output Cout
);

  and and_1 (Cout, A, B);
  xor xor_1 (S, A, B);
endmodule

module multiplicacao (
  input  A1,
  input  A0,
  input  B1,
  input  B0,
  output P3,
  output P2,
  output P1,
  output P0
);

  wire and_1_out, and_2_out, and_3_out, meiosomador_2_cout;

  and and_1 (and_1_out, A1, B1);
  meioSomador meiosomador_1 (.A(meiosomador_2_cout), .B(and_1_out), .S(P2), .Cout(P3));
  and and_2 (and_2_out, A1, B0);
  and and_3 (and_3_out, A0, B1);
  meioSomador meiosomador_2 (.A(and_3_out), .B(and_2_out), .S(P1), .Cout(meiosomador_2_cout));
  and and_4 (P0, A0, B0);
endmodule
