// Logisim project somar&subtrair.circ as structural Verilog: 3 circuits, main circuit main
module main (
  input  [3:0] A,
  input  [3:0] B,
  input  Cin,
  output Cout,
  output [3:0] S
);

  wire multiplexer_1_out, multiplexer_2_out, multiplexer_3_out, multiplexer_4_out, not_1_out, not_2_out,
       not_3_out, not_4_out, somadorcompleto_1_cout, somadorcompleto_2_cout, somadorcompleto_3_cout;

  not not_1 (not_1_out, B[0]);
  Multiplexer #(.enable("false")) multiplexer_1 (.in0(B[0]), .in1(not_1_out), .out(multiplexer_1_out), .sel(Cin));
  somadorCompleto somadorcompleto_1 (
    .A(A[0]), .B(multiplexer_1_out), .Cin(Cin), .S(S[0]), .Cout(somadorcompleto_1_cout));
  not not_2 (not_2_out, B[1]);
  Multiplexer #(.enable("false")) multiplexer_2 (.in0(B[1]), .in1(not_2_out), .out(multiplexer_2_out), .sel(Cin));
  not not_3 (not_3_out, B[2]);
  Multiplexer #(.enable("false")) multiplexer_3 (.in0(B[2]), .in1(not_3_out), .out(multiplexer_3_out), .sel(Cin));
  somadorCompleto somadorcompleto_2 (
    .A(A[1]), .B(multiplexer_2_out), .Cin(somadorcompleto_1_cout), .S(S[1]), .Cout(somadorcompleto_2_cout));
  somadorCompleto somadorcompleto_3 (
    .A(A[2]), .B(multiplexer_3_out), .Cin(somadorcompleto_2_cout), .S(S[2]), .Cout(somadorcompleto_3_cout));
  not not_4 (not_4_out, B[3]);
  Multiplexer #(.enable("false")) multiplexer_4 (.in0(B[3]), .in1(not_4_out), .out(multiplexer_4_out), .sel(Cin));
  somadorCompleto somadorcompleto_4 (
    .A(A[3]), .B(multiplexer_4_out), .Cin(somadorcompleto_3_cout), .S(S[3]), .Cout(Cout));
endmodule

module meioSomador (
  input  A,
  input  B,
  output S,
  output Cout
);

  and and_1 (Cout, A, B);
  xor xor_1 (S, A, B);
endmodule

module somadorCompleto (
  input  A,
  input  B,
  input  Cin,
  output S,
  output Cout
);

  wire meiosomador_1_cout, meiosomador_1_s, meiosomador_2_cout;

  meioSomador meiosomador_1 (.A(A), .B(B), .S(meiosomador_1_s), .Cout(meiosomador_1_cout));
  meioSomador meiosomador_2 (.A(meiosomador_1_s), .B(Cin), .S(S), .Cout(meiosomador_2_cout));
  or or_1 (Cout, meiosomador_2_cout, meiosomador_1_cout);
endmodule
