// Logisim project processadorFinal.circ as structural Verilog: 2 circuits, main circuit main
module main (
  input  Mem_to_Reg,
  input  Reset,
  input  [3:0] Alu_OP,
  input  Mem_R,
  input  Reg_W,
  input  Mem_W,
  input  Reg_Dest,
  input  Alu_Src
);

  wire aluSrc, CLK, memR, memtoreg, memW, regDest, registerfile_1_p7, regW, reset_t;
  wire [3:0] aluOP;
  wire [4:0] multiplexer_1_out;
  wire [5:0] funct, opcode;
  wire [25:6] mipsprogramrom_1_p2;
  wire [31:0] adder_1_out, bit_extender_1_out, mips_alu_1_p2, mips_alu_1_p4, mips_ram_1_p5, register_1_q,
       registerfile_1_p1, registerfile_1_p8;

  Clock clock_1 (.out(CLK));
  Register #(.width(32)) register_1 (.D(adder_1_out), .clk(CLK), .Q(register_1_q));  // open: en, clr
  Adder #(.width(32)) adder_1 (.a(register_1_q), .b(32'h4), .out(adder_1_out));  // open: cin, cout
  // MIPSProgramROM mipsprogramrom_1: pin names not known; wires that end beside it: register_1_q, {opcode, mipsprogramrom_1_p2, funct}
  Multiplexer #(.width(5), .enable("false")) multiplexer_1 (
    .in0(mipsprogramrom_1_p2[20:16]), .in1(mipsprogramrom_1_p2[15:11]), .out(multiplexer_1_out), .sel(regDest));
  assign bit_extender_1_out = {{16{mipsprogramrom_1_p2[15]}}, {mipsprogramrom_1_p2[15:6], funct}};  // Bit_Extender bit_extender_1
  // RegisterFile registerfile_1: pin names not known; wires that end beside it: registerfile_1_p1, CLK, regW, multiplexer_1_out, mipsprogramrom_1_p2[25:21], mipsprogramrom_1_p2[20:16], registerfile_1_p7, registerfile_1_p8
  // Mips_ALU mips_alu_1: pin names not known; wires that end beside it: registerfile_1_p7, mips_alu_1_p2, aluOP, mips_alu_1_p4, mips_alu_1_p4[19:0], registerfile_1_p8
  Multiplexer #(.width(32), .enable("false")) multiplexer_2 (
    .in0(bit_extender_1_out), .in1(registerfile_1_p8), .out(mips_alu_1_p2), .sel(aluSrc));
  ControlUnit controlunit_1 (
    .OPCODE(opcode), .FUNCT(funct), .Reg_Dest(regDest), .Reg_W(regW), .Alu_Src(aluSrc),
    .Mem_to_Reg(memtoreg), .Mem_W(memW), .Mem_R(memR), .Reset(reset_t), .Alu_OP(aluOP));
  Multiplexer #(.width(32), .enable("false")) multiplexer_3 (
    .in0(mips_alu_1_p4), .in1(mips_ram_1_p5), .out(registerfile_1_p1), .sel(memtoreg));
  // MIPS_RAM mips_ram_1: pin names not known; wires that end beside it: memW, CLK, memR, reset_t, mips_ram_1_p5

  // Notes on the sheet:
  //   000000 - opcode
  //   00001 - RS - $1
  //   00010 - RT - $2
  //   00011 - RD - $3
  //   00000 - SA
  //   100001 - funct - 0x21
  //   Reg_Dest -> 0 Tipo i // 1 Tipo R
  //   Reg_W -> 0 Desabilitado // 1 Habilitado
  //   Alu_Src -> 0 Tipo i // 1 Tipo R
  //   Mem_to_Reg -> 0 Tipo R // 1 Tipo i
  //   Ciclo de Busca da Instrução
  //   contents of mipsprogramrom_1 (hex, n*v repeats v):
  //   addiu $2, $0, 0x0011 or    $3, $1, $2  addiu $5, $0, 0x1001 xori  $7, $5, 0x0101
  //   Tipo R
  //   Tipo I
  //   Dado a ser escrito
  //   End. a ser escrito
  //   Linha de Write Back
endmodule

module ControlUnit (
  input  [5:0] OPCODE,
  input  [5:0] FUNCT,
  output Reg_Dest,
  output Reg_W,
  output Alu_Src,
  output Mem_to_Reg,
  output Mem_W,
  output Mem_R,
  output Reset,
  output [3:0] Alu_OP
);

  wire op_addiu_out, op_or_out;

  and op_addiu (op_addiu_out, ~OPCODE[5], ~OPCODE[4], OPCODE[3], ~OPCODE[2], ~OPCODE[1], OPCODE[0]);  // AND_Gate
  and op_or (op_or_out, ~OPCODE[5], ~OPCODE[4], ~OPCODE[3], ~OPCODE[2], ~OPCODE[1], ~OPCODE[0]);  // AND_Gate
  or or_1 (Reg_W, op_addiu_out, Alu_Src, Alu_OP[2]);
  and op_xori (Alu_OP[2], ~OPCODE[5], ~OPCODE[4], OPCODE[3], OPCODE[2], OPCODE[1], ~OPCODE[0]);  // AND_Gate
  and and_1 (Alu_Src, op_or_out, FUNCT[5], ~FUNCT[4], ~FUNCT[3], FUNCT[2], ~FUNCT[1], FUNCT[0]);  // AND_Gate
  or or_2 (Alu_OP[3], Alu_OP[2], Alu_Src);
  or or_3 (Alu_OP[1], op_addiu_out, Alu_Src);

  assign Alu_OP[0] = 1'b0;
  assign Mem_R = 1'b0;
  assign Mem_to_Reg = 1'b0;
  assign Mem_W = 1'b0;
  assign Reg_Dest = Alu_Src;
  assign Reset = 1'b0;
endmodule
