// Logisim project Projeto1_ALU_Juan_Carlos_GES_41.circ as structural Verilog: 11 circuits, main circuit main
module main (
  input  [7:0] A,
  input  [7:0] B,
  input  [2:0] in_3,
  input  [3:0] OP,
  output [7:0] S
);

  wire [7:0] adicao_1_s, e_and_1_s, nou_nor_1_s, ou_or_1_s, oux_xor_1_s, shifter_1_out, shifter_2_out,
       subtracao_1_s;

  nou_nor nou_nor_1 (.A(A), .B(B), .S(nou_nor_1_s));
  ouX_xor oux_xor_1 (.A(A), .B(B), .S(oux_xor_1_s));
  ou_or ou_or_1 (.A(A), .B(B), .S(ou_or_1_s));
  e_and e_and_1 (.A(A), .B(B), .S(e_and_1_s));
  Multiplexer #(.select(4), .width(8), .enable("false")) multiplexer_1 (
    .in0(adicao_1_s), .in1(shifter_1_out), .in2({8{1'b0}}), .in3(shifter_2_out), .in4(subtracao_1_s),
    .in5({8{1'b0}}), .in6(e_and_1_s), .in7(ou_or_1_s), .in8({8{1'b0}}), .in9({8{1'b0}}), .in10({8{1'b0}}),
    .in11(oux_xor_1_s), .in12({8{1'b0}}), .in13({8{1'b0}}), .in14(nou_nor_1_s), .in15({8{1'b0}}), .out(S),
    .sel(OP));
  adicao adicao_1 (.A(A), .B(B), .S(adicao_1_s));
  subtracao subtracao_1 (.A(A), .B(B), .S(subtracao_1_s));
  Shifter shifter_1 (.in(B), .\dist (in_3), .out(shifter_1_out));
  Shifter #(.shift("lr")) shifter_2 (.in(B), .\dist (in_3), .out(shifter_2_out));

  // Notes on the sheet:
  //   Adição - 0
  //   Desl. Esq. - 1
  //   Desl. Dir. - 3
  //   Subtração - 4
  //   E(AND) - 6
  //   OU(OR) - 7
  //   OU Exclusivo(XOR) - 11
  //   Ñ OU(NOR) - 14
endmodule

module meioSomador (
  input  A,
  input  B,
  output S,
  output Cout
);

  xor xor_1 (S, A, B);
  and and_1 (Cout, A, B);
endmodule

module somadorCompleto (
  input  A,
  input  B,
  input  Cin,
  output S,
  output Cout
);

  wire meiosomador_1_cout, meiosomador_1_s, meiosomador_2_cout;

  meioSomador meiosomador_1 (.A(A), .B(B), .S(meiosomador_1_s), .Cout(meiosomador_1_cout));
  meioSomador meiosomador_2 (.A(meiosomador_1_s), .B(Cin), .S(S), .Cout(meiosomador_2_cout));
  or or_1 (Cout, meiosomador_2_cout, meiosomador_1_cout);
endmodule

module adicao (
  input  [7:0] A,
  input  [7:0] B,
  output [7:0] S
);

  wire somadorcompleto_2_cout, somadorcompleto_3_cout, somadorcompleto_4_cout, somadorcompleto_5_cout,
       somadorcompleto_6_cout, somadorcompleto_7_cout, somadorcompleto_8_cout;

  somadorCompleto somadorcompleto_1 (.A(A[7]), .B(B[7]), .Cin(somadorcompleto_2_cout), .S(S[7]));  // open: Cout
  somadorCompleto somadorcompleto_2 (
    .A(A[6]), .B(B[6]), .Cin(somadorcompleto_3_cout), .S(S[6]), .Cout(somadorcompleto_2_cout));
  somadorCompleto somadorcompleto_3 (
    .A(A[5]), .B(B[5]), .Cin(somadorcompleto_4_cout), .S(S[5]), .Cout(somadorcompleto_3_cout));
  somadorCompleto somadorcompleto_4 (
    .A(A[4]), .B(B[4]), .Cin(somadorcompleto_5_cout), .S(S[4]), .Cout(somadorcompleto_4_cout));
  somadorCompleto somadorcompleto_5 (
    .A(A[3]), .B(B[3]), .Cin(somadorcompleto_6_cout), .S(S[3]), .Cout(somadorcompleto_5_cout));
  somadorCompleto somadorcompleto_6 (
    .A(A[2]), .B(B[2]), .Cin(somadorcompleto_7_cout), .S(S[2]), .Cout(somadorcompleto_6_cout));
  somadorCompleto somadorcompleto_7 (
    .A(A[1]), .B(B[1]), .Cin(somadorcompleto_8_cout), .S(S[1]), .Cout(somadorcompleto_7_cout));
  somadorCompleto somadorcompleto_8 (.A(A[0]), .B(B[0]), .Cin(1'b0), .S(S[0]), .Cout(somadorcompleto_8_cout));
endmodule

module meioSubtrator (
  input  A,
  input  B,
  output S,
  output Tout
);

  xor xor_1 (S, A, B);
  and and_1 (Tout, ~A, B);  // AND_Gate
endmodule

module subtratorCompleto (
  input  A,
  input  B,
  input  Tin,
  output S,
  output Tout
);

  wire meiosubtrator_1_s, meiosubtrator_1_tout, meiosubtrator_2_tout;

  meioSubtrator meiosubtrator_1 (.A(A), .B(B), .S(meiosubtrator_1_s), .Tout(meiosubtrator_1_tout));
  meioSubtrator meiosubtrator_2 (.A(meiosubtrator_1_s), .B(Tin), .S(S), .Tout(meiosubtrator_2_tout));
  or or_1 (Tout, meiosubtrator_2_tout, meiosubtrator_1_tout);
endmodule

module subtracao (
  input  [7:0] A,
  input  [7:0] B,
  output [7:0] S
);

  wire subtratorcompleto_2_tout, subtratorcompleto_3_tout, subtratorcompleto_4_tout,
       subtratorcompleto_5_tout, subtratorcompleto_6_tout, subtratorcompleto_7_tout, subtratorcompleto_8_tout;

  subtratorCompleto subtratorcompleto_1 (.A(A[7]), .B(B[7]), .Tin(subtratorcompleto_2_tout), .S(S[7]));  // open: Tout
  subtratorCompleto subtratorcompleto_2 (
    .A(A[6]), .B(B[6]), .Tin(subtratorcompleto_3_tout), .S(S[6]), .Tout(subtratorcompleto_2_tout));
  subtratorCompleto subtratorcompleto_3 (
    .A(A[5]), .B(B[5]), .Tin(subtratorcompleto_4_tout), .S(S[5]), .Tout(subtratorcompleto_3_tout));
  subtratorCompleto subtratorcompleto_4 (
    .A(A[4]), .B(B[4]), .Tin(subtratorcompleto_5_tout), .S(S[4]), .Tout(subtratorcompleto_4_tout));
  subtratorCompleto subtratorcompleto_5 (
    .A(A[3]), .B(B[3]), .Tin(subtratorcompleto_6_tout), .S(S[3]), .Tout(subtratorcompleto_5_tout));
  subtratorCompleto subtratorcompleto_6 (
    .A(A[2]), .B(B[2]), .Tin(subtratorcompleto_7_tout), .S(S[2]), .Tout(subtratorcompleto_6_tout));
  subtratorCompleto subtratorcompleto_7 (
    .A(A[1]), .B(B[1]), .Tin(subtratorcompleto_8_tout), .S(S[1]), .Tout(subtratorcompleto_7_tout));
  subtratorCompleto subtratorcompleto_8 (.A(A[0]), .B(B[0]), .Tin(1'b0), .S(S[0]), .Tout(subtratorcompleto_8_tout));
endmodule

module e_and (
  input  [7:0] A,
  input  [7:0] B,
  output [7:0] S
);

  and and_1 (S[7], A[7], B[7]);
  and and_2 (S[6], A[6], B[6]);
  and and_3 (S[5], A[5], B[5]);
  and and_4 (S[4], A[4], B[4]);
  and and_5 (S[3], A[3], B[3]);
  and and_6 (S[2], A[2], B[2]);
  and and_7 (S[1], A[1], B[1]);
  and and_8 (S[0], A[0], B[0]);
endmodule

module ou_or (
  input  [7:0] A,
  input  [7:0] B,
  output [7:0] S
);

  or or_1 (S[7], A[7], B[7]);
  or or_2 (S[6], A[6], B[6]);
  or or_3 (S[5], A[5], B[5]);
  or or_4 (S[4], A[4], B[4]);
  or or_5 (S[3], A[3], B[3]);
  or or_6 (S[2], A[2], B[2]);
  or or_7 (S[1], A[1], B[1]);
  or or_8 (S[0], A[0], B[0]);
endmodule

module ouX_xor (
  input  [7:0] A,
  input  [7:0] B,
  output [7:0] S
);

  xor xor_1 (S[7], A[7], B[7]);
  xor xor_2 (S[6], A[6], B[6]);
  xor xor_3 (S[5], A[5], B[5]);
  xor xor_4 (S[4], A[4], B[4]);
  xor xor_5 (S[3], A[3], B[3]);
  xor xor_6 (S[2], A[2], B[2]);
  xor xor_7 (S[1], A[1], B[1]);
  xor xor_8 (S[0], A[0], B[0]);
endmodule

module nou_nor (
  input  [7:0] A,
  input  [7:0] B,
  output [7:0] S
);

  xnor xnor_1 (S[7], A[7], B[7]);
  xnor xnor_2 (S[6], A[6], B[6]);
  xnor xnor_3 (S[5], A[5], B[5]);
  xnor xnor_4 (S[4], A[4], B[4]);
  xnor xnor_5 (S[3], A[3], B[3]);
  xnor xnor_6 (S[2], A[2], B[2]);
  xnor xnor_7 (S[1], A[1], B[1]);
  xnor xnor_8 (S[0], A[0], B[0]);
endmodule
