// Logisim project processador.circ as structural Verilog: 1 circuit, main circuit main
module main (
  input  Mem_to_Reg,
  input  Reset,
  input  [3:0] Alu_OP,
  input  Mem_W,
  input  Mem_R,
  input  Alu_Src,
  input  Reg_W,
  input  Reg_Dest
);

  wire CLK, registerfile_1_p7;
  wire [4:0] multiplexer_1_out;
  wire [31:0] adder_1_out, bit_extender_1_out, mips_alu_1_p2, mips_alu_1_p4, mips_ram_1_p5,
       mipsprogramrom_1_p2, register_1_q, registerfile_1_p1, registerfile_1_p8;

  Clock clock_1 (.out(CLK));
  Register #(.width(32)) register_1 (.D(adder_1_out), .clk(CLK), .Q(register_1_q));  // open: en, clr
  Adder #(.width(32)) adder_1 (.a(register_1_q), .b(32'h4), .out(adder_1_out));  // open: cin, cout
  // MIPSProgramROM mipsprogramrom_1: pin names not known; wires that end beside it: register_1_q, mipsprogramrom_1_p2
  Multiplexer #(.width(5), .enable("false")) multiplexer_1 (
    .in0(mipsprogramrom_1_p2[20:16]), .in1(mipsprogramrom_1_p2[15:11]), .out(multiplexer_1_out),
    .sel(Reg_Dest));
  assign bit_extender_1_out = {{16{mipsprogramrom_1_p2[15]}}, mipsprogramrom_1_p2[15:0]};  // Bit_Extender bit_extender_1
  // RegisterFile registerfile_1: pin names not known; wires that end beside it: registerfile_1_p1, CLK, Reg_W, multiplexer_1_out, mipsprogramrom_1_p2[25:21], mipsprogramrom_1_p2[20:16], registerfile_1_p7, registerfile_1_p8
  // Mips_ALU mips_alu_1: pin names not known; wires that end beside it: registerfile_1_p7, mips_alu_1_p2, Alu_OP, mips_alu_1_p4, mips_alu_1_p4[19:0], bit_extender_1_out
  Multiplexer #(.width(32), .enable("false")) multiplexer_2 (
    .in0(bit_extender_1_out), .in1(registerfile_1_p8), .out(mips_alu_1_p2), .sel(Alu_Src));
  Multiplexer #(.width(32), .enable("false")) multiplexer_3 (
    .in0(mips_alu_1_p4), .in1(mips_ram_1_p5), .out(registerfile_1_p1), .sel(Mem_to_Reg));
  // MIPS_RAM mips_ram_1: pin names not known; wires that end beside it: Mem_W, CLK, Mem_R, Reset, mips_ram_1_p5

  // Notes on the sheet:
  //   000000 - opcode
  //   00001 - RS - $1
  //   00010 - RT - $2
  //   00011 - RD - $3
  //   00000 - SA
  //   100001 - funct - 0x21
  //   Reg_Dest -> 0 Tipo i // 1 Tipo R
  //   Reg_W -> 0 Desabilitado // 1 Habilitado
  //   Alu_Src -> 0 Tipo i // 1 Tipo R
  //   Mem_to_Reg -> 0 Tipo R // 1 Tipo i
  //   Ciclo de Busca da Instrução
  //   contents of mipsprogramrom_1 (hex, n*v repeats v):
  //   addiu $2, $2, 0x0020 addu $3, $1, $2
  //   Tipo R
  //   Tipo I
  //   Dado a ser escrito
  //   End. a ser escrito
  //   Linha de Write Back
endmodule
